// Logisim project 4-bit adder.circ as structural Verilog: 3 circuits, main circuit FA
module FA (
  input  x,
  input  y,
  output sum,
  output carry
);

  xor xor_1 (sum, x, y);
  and and_1 (carry, x, y);
endmodule

module CinFA (
  input  Cin,
  input  x,
  input  y,
  output sum,
  output Cout
);

  wire and_1_out, and_2_out, and_3_out, and_4_out, xor_1_out;

  and and_1 (and_1_out, y, x);
  and and_2 (and_2_out, x, Cin);
  or or_1 (Cout, and_1_out, and_2_out, and_3_out);
  ExactlyOne xor_1 (.out(xor_1_out), .in0(Cin), .in2(x), .in4(y));
  and and_3 (and_3_out, y, Cin);
  and and_4 (and_4_out, Cin, x, y);
  or or_2 (sum, xor_1_out, and_4_out);
endmodule

module _4bitFA (
  input  x0,
  input  x1,
  input  x2,
  input  x3,
  input  y0,
  input  y1,
  input  y2,
  input  y2_2,
  output z0,
  output z1,
  output z2,
  output z3,
  output overflow
);

  wire cinfa_1_cout, cinfa_2_cout, cinfa_3_cout;

  CinFA cinfa_1 (.x(x0), .y(y0), .Cin(1'b0), .Cout(cinfa_1_cout), .sum(z0));
  CinFA cinfa_2 (.x(x1), .y(y1), .Cin(cinfa_1_cout), .Cout(cinfa_2_cout), .sum(z1));
  CinFA cinfa_3 (.x(x2), .y(y2), .Cin(cinfa_2_cout), .Cout(cinfa_3_cout), .sum(z2));
  CinFA cinfa_4 (.x(x3), .y(y2_2), .Cin(cinfa_3_cout), .Cout(overflow), .sum(z3));
endmodule
