// Logisim project GabeH_ALU.circ as structural Verilog: 7 circuits, main circuit main
module main (
  input  fin,
  input  noin,
  input  zxin,
  input  nxin,
  input  zyin,
  input  nyin,
  input  x0,
  input  x1,
  input  x2,
  input  x3,
  input  y0,
  input  y1,
  input  y2,
  input  y3,
  output out0,
  output out1,
  output out2,
  output out3
);

  wire f_1_out0, f_1_out1, f_1_out2, f_1_out3, nx_1_x0out, nx_1_x1out, nx_1_x2out, nx_1_x3out, nx_1_y0out,
       nx_1_y1out, nx_1_y2out, nx_1_y3out, ny_1_x0out, ny_1_x1out, ny_1_x2out, ny_1_x3out, ny_1_y0out,
       ny_1_y1out, ny_1_y2out, ny_1_y3out, zx_1_x0out, zx_1_x1out, zx_1_x2out, zx_1_x3out, zx_1_y0out,
       zx_1_y1out, zx_1_y2out, zx_1_y3out, zy_1_x0out, zy_1_x1out, zy_1_x2out, zy_1_x3out, zy_1_y0out,
       zy_1_y1out, zy_1_y2out, zy_1_y3out;

  zx zx_1 (
    .zxin(zxin), .x0(x0), .x1(x1), .x2(x2), .x3(x3), .y0(y0), .y1(y1), .y2(y2), .y3(y3), .x0out(zx_1_x0out),
    .x1out(zx_1_x1out), .x2out(zx_1_x2out), .x3out(zx_1_x3out), .y0out(zx_1_y0out), .y1out(zx_1_y1out),
    .y2out(zx_1_y2out), .y3out(zx_1_y3out));
  nx nx_1 (
    .nxin(nxin), .x0(zx_1_x0out), .x1(zx_1_x1out), .x2(zx_1_x2out), .x3(zx_1_x3out), .y0(zx_1_y0out),
    .y1(zx_1_y1out), .y2(zx_1_y2out), .y3(zx_1_y3out), .x0out(nx_1_x0out), .x1out(nx_1_x1out),
    .x2out(nx_1_x2out), .x3out(nx_1_x3out), .y0out(nx_1_y0out), .y1out(nx_1_y1out), .y2out(nx_1_y2out),
    .y3out(nx_1_y3out));
  zy zy_1 (
    .zyin(zyin), .x0(nx_1_x0out), .x1(nx_1_x1out), .x2(nx_1_x2out), .x3(nx_1_x3out), .y0(nx_1_y0out),
    .y1(nx_1_y1out), .y2(nx_1_y2out), .y3(nx_1_y3out), .x0out(zy_1_x0out), .x1out(zy_1_x1out),
    .x2out(zy_1_x2out), .x3out(zy_1_x3out), .y0out(zy_1_y0out), .y1out(zy_1_y1out), .y2out(zy_1_y2out),
    .y3out(zy_1_y3out));
  ny ny_1 (
    .nyin(nyin), .x0(zy_1_x0out), .x1(zy_1_x1out), .x2(zy_1_x2out), .x3(zy_1_x3out), .y0(zy_1_y0out),
    .y1(zy_1_y1out), .y2(zy_1_y2out), .y3(zy_1_y3out), .x0out(ny_1_x0out), .x1out(ny_1_x1out),
    .x2out(ny_1_x2out), .x3out(ny_1_x3out), .y0out(ny_1_y0out), .y1out(ny_1_y1out), .y2out(ny_1_y2out),
    .y3out(ny_1_y3out));
  f f_1 (
    .fin(fin), .x0(ny_1_x0out), .x1(ny_1_x1out), .x2(ny_1_x2out), .x3(ny_1_x3out), .y0(ny_1_y0out),
    .y1(ny_1_y1out), .y2(ny_1_y2out), .y3(ny_1_y3out), .out0(f_1_out0), .out1(f_1_out1), .out2(f_1_out2),
    .out3(f_1_out3));
  no no_1 (
    .noin(noin), .in0(f_1_out0), .in1(f_1_out1), .in2(f_1_out2), .in3(f_1_out3), .out0(out0), .out1(out1),
    .out2(out2), .out3(out3));

  // Notes on the sheet:
  //   Gabe Howland
  //   Inputs
  //   control
endmodule

module zx (
  input  zxin,
  input  x0,
  input  x1,
  input  x2,
  input  x3,
  input  y0,
  input  y1,
  input  y2,
  input  y3,
  output x0out,
  output x1out,
  output x2out,
  output x3out,
  output y0out,
  output y1out,
  output y2out,
  output y3out
);

  wire not_1_out;

  not not_1 (not_1_out, zxin);
  Multiplexer multiplexer_1 (.in0(x0), .in1(not_1_out), .out(x0out), .sel(zxin));
  Multiplexer multiplexer_2 (.in0(x1), .in1(not_1_out), .out(x1out), .sel(zxin));
  Multiplexer multiplexer_3 (.in0(x2), .in1(not_1_out), .out(x2out), .sel(zxin));
  Multiplexer multiplexer_4 (.in0(x3), .in1(not_1_out), .out(x3out), .sel(zxin));

  assign y0out = y0;
  assign y1out = y1;
  assign y2out = y2;
  assign y3out = y3;
endmodule

module nx (
  input  nxin,
  input  x0,
  input  x1,
  input  x2,
  input  x3,
  input  y0,
  input  y1,
  input  y2,
  input  y3,
  output x0out,
  output x1out,
  output x2out,
  output x3out,
  output y0out,
  output y1out,
  output y2out,
  output y3out
);

  wire and_1_out, and_2_out, and_3_out, and_4_out, and_5_out, and_6_out, and_7_out, and_8_out, not_1_out,
       not_2_out, not_3_out, not_4_out, not_5_out, not_6_out, not_7_out, not_8_out;

  not not_1 (not_1_out, x0);
  not not_2 (not_2_out, x1);
  not not_3 (not_3_out, x2);
  not not_4 (not_4_out, x3);
  not not_5 (not_5_out, nxin);
  not not_6 (not_6_out, nxin);
  not not_7 (not_7_out, nxin);
  not not_8 (not_8_out, nxin);
  and and_1 (and_1_out, nxin, x0);
  and and_2 (and_2_out, not_5_out, not_1_out);
  and and_3 (and_3_out, nxin, x1);
  and and_4 (and_4_out, not_6_out, not_2_out);
  and and_5 (and_5_out, nxin, x2);
  and and_6 (and_6_out, not_7_out, not_3_out);
  and and_7 (and_7_out, nxin, x3);
  and and_8 (and_8_out, not_8_out, not_4_out);
  nor nor_1 (x0out, and_1_out, and_2_out);
  nor nor_2 (x1out, and_3_out, and_4_out);
  nor nor_3 (x2out, and_5_out, and_6_out);
  nor nor_4 (x3out, and_7_out, and_8_out);

  assign y0out = y0;
  assign y1out = y1;
  assign y2out = y2;
  assign y3out = y3;
endmodule

module zy (
  input  zyin,
  input  x0,
  input  x1,
  input  x2,
  input  x3,
  input  y0,
  input  y1,
  input  y2,
  input  y3,
  output x0out,
  output x1out,
  output x2out,
  output x3out,
  output y0out,
  output y1out,
  output y2out,
  output y3out
);

  wire not_1_out;

  not not_1 (not_1_out, zyin);
  Multiplexer multiplexer_1 (.in0(y0), .in1(not_1_out), .out(y0out), .sel(zyin));
  Multiplexer multiplexer_2 (.in0(y1), .in1(not_1_out), .out(y1out), .sel(zyin));
  Multiplexer multiplexer_3 (.in0(y2), .in1(not_1_out), .out(y2out), .sel(zyin));
  Multiplexer multiplexer_4 (.in0(y3), .in1(not_1_out), .out(y3out), .sel(zyin));

  assign x0out = x0;
  assign x1out = x1;
  assign x2out = x2;
  assign x3out = x3;
endmodule

module ny (
  input  nyin,
  input  x0,
  input  x1,
  input  x2,
  input  x3,
  input  y0,
  input  y1,
  input  y2,
  input  y3,
  output x0out,
  output x1out,
  output x2out,
  output x3out,
  output y0out,
  output y1out,
  output y2out,
  output y3out
);

  wire and_1_out, and_2_out, and_3_out, and_4_out, and_5_out, and_6_out, and_7_out, and_8_out, not_1_out,
       not_2_out, not_3_out, not_4_out, not_5_out, not_6_out, not_7_out, not_8_out;

  not not_1 (not_1_out, y0);
  not not_2 (not_2_out, y1);
  not not_3 (not_3_out, y2);
  not not_4 (not_4_out, y3);
  not not_5 (not_5_out, nyin);
  not not_6 (not_6_out, nyin);
  not not_7 (not_7_out, nyin);
  not not_8 (not_8_out, nyin);
  and and_1 (and_1_out, nyin, y0);
  and and_2 (and_2_out, not_5_out, not_1_out);
  and and_3 (and_3_out, nyin, y1);
  and and_4 (and_4_out, not_6_out, not_2_out);
  and and_5 (and_5_out, nyin, y2);
  and and_6 (and_6_out, not_7_out, not_3_out);
  and and_7 (and_7_out, nyin, y3);
  and and_8 (and_8_out, not_8_out, not_4_out);
  nor nor_1 (y0out, and_1_out, and_2_out);
  nor nor_2 (y1out, and_3_out, and_4_out);
  nor nor_3 (y2out, and_5_out, and_6_out);
  nor nor_4 (y3out, and_7_out, and_8_out);

  assign x0out = x0;
  assign x1out = x1;
  assign x2out = x2;
  assign x3out = x3;
endmodule

module f (
  input  fin,
  input  x0,
  input  x1,
  input  x2,
  input  x3,
  input  y0,
  input  y1,
  input  y2,
  input  y3,
  output out0,
  output out1,
  output out2,
  output out3
);

  wire adder_1_cout, adder_1_out, adder_2_cout, adder_2_out, adder_3_cout, adder_3_out, adder_4_out,
       and_1_out, and_2_out, and_3_out, and_4_out, not_1_out;

  and and_1 (and_1_out, x0, y0);
  and and_2 (and_2_out, x1, y1);
  and and_3 (and_3_out, x2, y2);
  and and_4 (and_4_out, x3, y3);
  Adder #(.width(1)) adder_1 (.a(x0), .b(y0), .out(adder_1_out), .cin(1'b0), .cout(adder_1_cout));
  Adder #(.width(1)) adder_2 (.a(x1), .b(y1), .out(adder_2_out), .cin(adder_1_cout), .cout(adder_2_cout));
  Adder #(.width(1)) adder_3 (.a(x2), .b(y2), .out(adder_3_out), .cin(adder_2_cout), .cout(adder_3_cout));
  Adder #(.width(1)) adder_4 (.a(x3), .b(y3), .out(adder_4_out), .cin(adder_3_cout));  // open: cout
  Multiplexer multiplexer_1 (.in0(adder_3_out), .in1(and_3_out), .out(out2), .sel(not_1_out));
  Multiplexer multiplexer_2 (.in0(adder_4_out), .in1(and_4_out), .out(out3), .sel(not_1_out));
  not not_1 (not_1_out, fin);
  Multiplexer multiplexer_3 (.in0(adder_2_out), .in1(and_2_out), .out(out1), .sel(not_1_out));
  Multiplexer multiplexer_4 (.in0(adder_1_out), .in1(and_1_out), .out(out0), .sel(not_1_out));

  // Notes on the sheet:
  //   Addition
  //   Bitwise AND
endmodule

module no (
  input  noin,
  input  in0,
  input  in1,
  input  in2,
  input  in3,
  output out0,
  output out1,
  output out2,
  output out3
);

  wire and_1_out, and_2_out, and_3_out, and_4_out, and_5_out, and_6_out, and_7_out, and_8_out, not_1_out,
       not_2_out, not_3_out, not_4_out, not_5_out, not_6_out, not_7_out, not_8_out;

  not not_1 (not_1_out, in0);
  not not_2 (not_2_out, in1);
  not not_3 (not_3_out, in2);
  not not_4 (not_4_out, in3);
  not not_5 (not_5_out, noin);
  not not_6 (not_6_out, noin);
  not not_7 (not_7_out, noin);
  not not_8 (not_8_out, noin);
  and and_1 (and_1_out, noin, in0);
  and and_2 (and_2_out, not_5_out, not_1_out);
  and and_3 (and_3_out, noin, in1);
  and and_4 (and_4_out, not_6_out, not_2_out);
  and and_5 (and_5_out, noin, in2);
  and and_6 (and_6_out, not_7_out, not_3_out);
  and and_7 (and_7_out, noin, in3);
  and and_8 (and_8_out, not_8_out, not_4_out);
  nor nor_1 (out0, and_1_out, and_2_out);
  nor nor_2 (out1, and_3_out, and_4_out);
  nor nor_3 (out2, and_5_out, and_6_out);
  nor nor_4 (out3, and_7_out, and_8_out);
endmodule
