// Logisim project hw0p1.circ as structural Verilog: 1 circuit, main circuit main
module main (
  input  C0,
  input  C1,
  output D00,
  output D01,
  output D10,
  output D11
);

  wire not_1_out, not_2_out;

  not not_1 (not_1_out, C0);
  not not_2 (not_2_out, C1);
  and and_1 (D00, not_1_out, not_2_out);
  and and_2 (D01, C0, not_2_out);
  and and_3 (D10, not_1_out, C1);
  and and_4 (D11, C0, C1);

  // Notes on the sheet:
  //   Gabriel Howland
  //   HW0 Problem 1
endmodule
