// Logisim project hw0p2.circ as structural Verilog: 1 circuit, main circuit main
module main (
  input  X2,
  input  X1,
  input  X0,
  input  Y2,
  input  Y1,
  input  Y0,
  output out_7
);

  wire and_1_out, and_2_out, not_1_out, not_2_out;

  not not_1 (not_1_out, X0);
  not not_2 (not_2_out, Y0);
  and and_1 (and_1_out, X0, Y0);
  and and_2 (and_2_out, not_1_out, not_2_out);
  or or_1 (out_7, and_1_out, and_2_out);

  // Notes on the sheet:
  //   Gabriel Howland
  //   for 'x0' and 'y0' are the only determinates
  //   whether a number is odd or not
  //   compares if either number is odd
endmodule
