// Logisim project lab2.circ as structural Verilog: 3 circuits, main circuit fourbitneg
module fourbitneg (
  input  a0,
  input  a1,
  input  a2,
  input  a3,
  output out0,
  output out1,
  output out2,
  output out3
);

  wire adder_1_cout, adder_2_cout, adder_3_cout, not_1_out, not_2_out, not_3_out, not_4_out;

  not not_1 (not_1_out, a0);
  not not_2 (not_2_out, a1);
  not not_3 (not_3_out, a2);
  not not_4 (not_4_out, a3);
  Adder #(.width(1)) adder_1 (.a(not_1_out), .b(1'b0), .out(out0), .cin(1'b1), .cout(adder_1_cout));
  Adder #(.width(1)) adder_2 (.a(not_2_out), .b(1'b0), .out(out1), .cin(adder_1_cout), .cout(adder_2_cout));
  Adder #(.width(1)) adder_3 (.a(not_3_out), .b(1'b0), .out(out2), .cin(adder_2_cout), .cout(adder_3_cout));
  Adder #(.width(1)) adder_4 (.a(not_4_out), .b(1'b0), .out(out3), .cin(adder_3_cout));  // open: cout

  // Notes on the sheet:
  //   Gabe H
  //   Two's compliment converter
endmodule

module Subtract (
  input  a0,
  input  a1,
  input  a2,
  input  a3,
  input  b0,
  input  b1,
  input  b2,
  input  b3,
  output out_9,
  output out_10,
  output out_11,
  output out_12
);

  wire adder_1_cout, adder_2_cout, adder_3_cout, fourbitneg_1_out0, fourbitneg_1_out1, fourbitneg_1_out2,
       fourbitneg_1_out3;

  fourbitneg fourbitneg_1 (
    .a0(b0), .a1(b1), .a2(b2), .a3(b3), .out0(fourbitneg_1_out0), .out1(fourbitneg_1_out1),
    .out2(fourbitneg_1_out2), .out3(fourbitneg_1_out3));
  Adder #(.width(1)) adder_1 (.a(a0), .b(fourbitneg_1_out0), .out(out_9), .cin(1'b0), .cout(adder_1_cout));
  Adder #(.width(1)) adder_2 (.a(a1), .b(fourbitneg_1_out1), .out(out_10), .cin(adder_1_cout), .cout(adder_2_cout));
  Adder #(.width(1)) adder_3 (.a(a2), .b(fourbitneg_1_out2), .out(out_11), .cin(adder_2_cout), .cout(adder_3_cout));
  Adder #(.width(1)) adder_4 (.a(a3), .b(fourbitneg_1_out3), .out(out_12), .cin(adder_3_cout));  // open: cout

  // Notes on the sheet:
  //   Gabe H
endmodule

module comparitor (
  input  a0,
  input  a1,
  input  a2,
  input  a3,
  input  b0,
  input  b1,
  input  b2,
  input  b3,
  output out_9
);

  wire not_1_out, not_2_out, not_3_out, not_4_out, subtract_1_out_9, subtract_1_out_10, subtract_1_out_11,
       subtract_1_out_12;

  Subtract subtract_1 (
    .a0(a0), .a1(a1), .a2(a2), .a3(a3), .b0(b0), .b1(b1), .b2(b2), .b3(b3), .out_9(subtract_1_out_9),
    .out_10(subtract_1_out_10), .out_11(subtract_1_out_11), .out_12(subtract_1_out_12));
  not not_1 (not_1_out, subtract_1_out_9);
  not not_2 (not_2_out, subtract_1_out_10);
  not not_3 (not_3_out, subtract_1_out_11);
  not not_4 (not_4_out, subtract_1_out_12);
  // AND_Gate and_1: pin names not known; wires that end beside it: not_1_out, not_2_out, not_3_out, not_4_out, out_9

  // Notes on the sheet:
  //   Gabe H
  //   comparator
endmodule
