// Logisim project mux4.circ as structural Verilog: 1 circuit, main circuit main
module main (
  input  line00,
  input  line01,
  input  line02,
  input  line03,
  input  select0,
  input  select1,
  output out_7
);

  wire and_1_out, and_2_out, and_3_out, and_4_out, and_5_out, and_6_out, and_7_out, and_8_out, not_1_out,
       not_2_out;

  not not_1 (not_1_out, select0);
  not not_2 (not_2_out, select1);
  and and_1 (and_1_out, not_1_out, not_2_out);
  and and_2 (and_2_out, select0, not_2_out);
  and and_3 (and_3_out, not_1_out, select1);
  and and_4 (and_4_out, select0, select1);
  and and_5 (and_5_out, line00, and_1_out);
  and and_6 (and_6_out, line02, and_3_out);
  and and_7 (and_7_out, line01, and_2_out);
  and and_8 (and_8_out, line03, and_4_out);
  or or_1 (out_7, and_5_out, and_7_out, and_6_out, and_8_out);

  // Notes on the sheet:
  //   Mux Circuit
  //   Gabriel Howland
endmodule
