// Logisim project parity.circ as structural Verilog: 1 circuit, main circuit main
module main (
  input  X,
  input  Y,
  input  Z,
  output out_4
);

  wire and_1_out, and_2_out, and_3_out, and_5_out, not_1_out, not_2_out, not_3_out;

  not not_1 (not_1_out, X);
  not not_2 (not_2_out, Y);
  not not_3 (not_3_out, Z);
  and and_1 (and_1_out, X, not_2_out, not_3_out);
  and and_2 (and_2_out, not_3_out, Y, not_1_out);
  and and_3 (and_3_out, Z, not_2_out, not_1_out);
  and and_4 (and_3_out, Z, not_2_out, not_1_out);
  and and_5 (and_5_out, Z, Y, X);
  or or_1 (out_4, and_1_out, and_2_out, and_3_out, and_5_out);

  // Notes on the sheet:
  //   Gabriel Howland
  //   Lab0 'Parity'
endmodule
