// Logisim project sm_evolution.circ as structural Verilog: 3 circuits, main circuit main
module main (
  input  \input ,
  input  clear,
  output just_saw_101
);

  wire clock_1_out;
  wire [1:0] next_1_s0_out, register_1_q;

  next next_1 (
    .\input (\input ), .s1(register_1_q[1]), .s0(register_1_q[0]), .s1_out(next_1_s0_out[1]),
    .s0_out(next_1_s0_out[0]));
  Clock clock_1 (.out(clock_1_out));
  Register #(.width(2)) register_1 (.D(next_1_s0_out), .en(1'b1), .Q(register_1_q), .clk(clock_1_out), .clr(clear));
  out out_1 (.s1(register_1_q[1]), .s0(register_1_q[0]), .\output (just_saw_101));
endmodule

module next (
  input  \input ,
  input  s1,
  input  s0,
  output s1_out,
  output s0_out
);
endmodule

module out (
  input  s1,
  input  s0,
  output \output 
);
endmodule
